// Logisim project pcu6.circ as structural Verilog: 1 circuit, main circuit main
module main (
);

  wire adder_1_cout, and_1_out, and_2_out, and_4_out, and_5_out, and_6_out, and_7_out, and_8_out, and_9_out,
       and_10_out, and_11_out, button_1_out, button_2_out, clock_1_out, d_ff_1_q, d_ff_2_q, d_ff_3_q,
       demultiplexer_1_out0, demultiplexer_1_out1, demultiplexer_1_out2, demultiplexer_1_out3,
       demultiplexer_2_out0, demultiplexer_2_out1, demultiplexer_2_out2, demultiplexer_2_out3,
       demultiplexer_2_out4, demultiplexer_2_out5, demultiplexer_2_out6, demultiplexer_2_out7,
       demultiplexer_2_out10, demultiplexer_2_out11, demultiplexer_2_out12, demultiplexer_2_out13,
       demultiplexer_3_out0, demultiplexer_3_out1, demultiplexer_3_out2, demultiplexer_3_out3,
       demultiplexer_3_out4, demultiplexer_3_out5, demultiplexer_3_out6, demultiplexer_3_out7, nor_2_out,
       nor_3_out, not_1_out, or_1_out, or_2_out, or_3_out, or_4_out, or_5_out, or_6_out, or_7_out, or_9_out,
       or_10_out, or_11_out, or_12_out, or_13_out, xor_1_out, xor_2_out;
  wire [0:0] counter_1_q;
  wire [1:1] counter_1_q_2;
  wire [6:0] bit_extender_1_out;
  wire [7:0] adder_1_out, and_3_out, controlled_buffer_3_out, controlled_buffer_5_out,
       controlled_buffer_6_out, counter_2_q, counter_3_q, nor_1_out, or_8_out, ram_1_dout, register_1_q,
       register_2_q, register_3_q, register_4_q, rom_1_data;
  wire [9:0] controlled_buffer_1_out;

  Clock clock_1 (.out(clock_1_out));
  assign controlled_buffer_1_out = or_1_out ? {1'b0, counter_3_q, counter_1_q[0]} : 10'bz;  // Controlled_Buffer controlled_buffer_1
  Counter #(.max('h3), .width(2)) counter_1 (
    .clr(button_2_out), .load(1'b0), .up(1'b1), .count(1'b1), .clk(clock_1_out),
    .Q({counter_1_q_2[1], counter_1_q[0]}));  // open: D, carry
  ROM #(.addrWidth(10)) rom_1 (.addr(controlled_buffer_1_out), .data(rom_1_data));
  assign controlled_buffer_1_out = demultiplexer_1_out2 ? {2'b10, controlled_buffer_5_out} : 10'bz;  // Controlled_Buffer controlled_buffer_2
  or or_1 (or_1_out, demultiplexer_1_out1, demultiplexer_1_out0);
  Demultiplexer #(.select(2)) demultiplexer_1 (
    .out0(demultiplexer_1_out0), .out1(demultiplexer_1_out1), .out2(demultiplexer_1_out2),
    .out3(demultiplexer_1_out3), .in(1'b1), .sel({counter_1_q_2[1], counter_1_q[0]}));
  Register register_1 (
    .D(rom_1_data), .en(demultiplexer_1_out0), .clk(clock_1_out), .Q(register_1_q), .clr(button_2_out));
  Register register_2 (
    .D(rom_1_data), .en(demultiplexer_1_out1), .clk(clock_1_out), .Q(register_2_q), .clr(button_2_out));
  Demultiplexer #(.select(4)) demultiplexer_2 (
    .out0(demultiplexer_2_out0), .out1(demultiplexer_2_out1), .out2(demultiplexer_2_out2),
    .out3(demultiplexer_2_out3), .out4(demultiplexer_2_out4), .out5(demultiplexer_2_out5),
    .out6(demultiplexer_2_out6), .out7(demultiplexer_2_out7), .out10(demultiplexer_2_out10),
    .out11(demultiplexer_2_out11), .out12(demultiplexer_2_out12), .out13(demultiplexer_2_out13),
    .in(demultiplexer_1_out2), .sel(register_2_q[3:0]));  // open: out8, out9, out14, out15
  or or_2 (or_2_out, demultiplexer_2_out0, demultiplexer_2_out1, demultiplexer_2_out2, demultiplexer_2_out3, demultiplexer_2_out4, demultiplexer_2_out5);
  or or_3 (or_3_out, or_2_out, demultiplexer_2_out6);
  assign controlled_buffer_3_out = or_5_out ? rom_1_data : 8'bz;  // Controlled_Buffer controlled_buffer_3
  or or_4 (or_4_out, demultiplexer_2_out10, demultiplexer_2_out11);
  Demultiplexer #(.select(3)) demultiplexer_3 (
    .out0(demultiplexer_3_out0), .out1(demultiplexer_3_out1), .out2(demultiplexer_3_out2),
    .out3(demultiplexer_3_out3), .out4(demultiplexer_3_out4), .out5(demultiplexer_3_out5),
    .out6(demultiplexer_3_out6), .out7(demultiplexer_3_out7), .in(or_3_out), .sel(register_2_q[6:4]));
  or or_5 (or_5_out, demultiplexer_2_out12, demultiplexer_2_out13);
  Counter counter_2 (
    .clr(button_2_out), .load(demultiplexer_2_out2), .up(demultiplexer_2_out10), .count(or_4_out),
    .clk(clock_1_out), .D(controlled_buffer_3_out), .Q(counter_2_q));  // open: carry
  assign controlled_buffer_3_out = demultiplexer_3_out0 ? register_1_q : 8'bz;  // Controlled_Buffer controlled_buffer_4
  or or_6 (or_6_out, demultiplexer_2_out0, demultiplexer_2_out12);
  or or_7 (or_7_out, demultiplexer_2_out1, demultiplexer_2_out13);
  Register register_3 (
    .D(controlled_buffer_3_out), .en(or_6_out), .clk(clock_1_out), .Q(register_3_q), .clr(button_2_out));
  Register register_4 (
    .D(controlled_buffer_3_out), .en(or_7_out), .clk(clock_1_out), .Q(register_4_q), .clr(button_2_out));
  assign controlled_buffer_5_out = register_2_q[7] ? counter_2_q : 8'bz;  // Controlled_Buffer controlled_buffer_5
  assign controlled_buffer_6_out = register_2_q[7] ? register_4_q : 8'bz;  // Controlled_Buffer controlled_buffer_6
  not not_1 (not_1_out, register_2_q[7]);
  assign controlled_buffer_6_out = not_1_out ? register_1_q : 8'bz;  // Controlled_Buffer controlled_buffer_7
  assign controlled_buffer_5_out = not_1_out ? register_1_q : 8'bz;  // Controlled_Buffer controlled_buffer_8
  RAM #(.asyncread("true")) ram_1 (
    .addr(controlled_buffer_5_out), .we(demultiplexer_2_out3), .oe(demultiplexer_3_out7), .clk(and_1_out),
    .din(controlled_buffer_3_out), .dout(ram_1_dout));
  and and_1 (and_1_out, clock_1_out, ~and_2_out);  // AND_Gate
  and and_2 (and_2_out, controlled_buffer_5_out[0], controlled_buffer_5_out[1], controlled_buffer_5_out[2], controlled_buffer_5_out[3], controlled_buffer_5_out[4], controlled_buffer_5_out[5], controlled_buffer_5_out[6], controlled_buffer_5_out[7]);
  Adder adder_1 (.a(register_3_q), .b(controlled_buffer_6_out), .out(adder_1_out), .cin(d_ff_1_q), .cout(adder_1_cout));
  assign and_3_out = register_3_q & controlled_buffer_6_out;  // AND_Gate and_3, 8 bits wide
  assign or_8_out = register_3_q | controlled_buffer_6_out;  // OR_Gate or_8, 8 bits wide
  assign nor_1_out = ~(register_3_q | controlled_buffer_6_out);  // NOR_Gate nor_1, 8 bits wide
  Bit_Extender #(.out_width(7)) bit_extender_1 (.in(controlled_buffer_3_out), .out(bit_extender_1_out));
  and and_4 (and_4_out, and_2_out, demultiplexer_2_out3);
  and and_5 (and_5_out, demultiplexer_2_out5, d_ff_3_q);
  or or_9 (or_9_out, demultiplexer_2_out4, and_5_out);
  Counter counter_3 (
    .clr(button_2_out), .load(or_9_out), .up(1'b1), .count(demultiplexer_1_out3), .clk(clock_1_out),
    .D(controlled_buffer_3_out), .Q(counter_3_q));  // open: carry
  assign controlled_buffer_3_out = demultiplexer_3_out3 ? adder_1_out : 8'bz;  // Controlled_Buffer controlled_buffer_9
  assign controlled_buffer_3_out = demultiplexer_3_out4 ? and_3_out : 8'bz;  // Controlled_Buffer controlled_buffer_10
  assign controlled_buffer_3_out = demultiplexer_3_out5 ? or_8_out : 8'bz;  // Controlled_Buffer controlled_buffer_11
  assign controlled_buffer_3_out = demultiplexer_3_out6 ? nor_1_out : 8'bz;  // Controlled_Buffer controlled_buffer_12
  assign controlled_buffer_3_out = demultiplexer_3_out1 ? register_3_q : 8'bz;  // Controlled_Buffer controlled_buffer_13
  assign controlled_buffer_3_out = demultiplexer_3_out2 ? register_4_q : 8'bz;  // Controlled_Buffer controlled_buffer_14
  TTY #(.cols(40)) tty_1 (.data(bit_extender_1_out), .clk(clock_1_out), .we(and_4_out), .clr(button_1_out));
  Button button_1 (.out(button_1_out));
  assign controlled_buffer_3_out = demultiplexer_3_out7 ? ram_1_dout : 8'bz;  // Controlled_Buffer controlled_buffer_15
  D_Flip_Flop d_ff_1 (
    .D(adder_1_cout), .clk(demultiplexer_3_out3), .Q(d_ff_1_q), .reset(button_2_out));  // open: Qn, preset
  or or_10 (or_10_out, demultiplexer_2_out12, demultiplexer_2_out13, or_3_out);
  and and_6 (and_6_out, clock_1_out, or_10_out);
  and and_7 (and_7_out, or_10_out, nor_2_out);
  nor nor_2 (nor_2_out, controlled_buffer_3_out[0], controlled_buffer_3_out[1], controlled_buffer_3_out[2], controlled_buffer_3_out[3], controlled_buffer_3_out[4], controlled_buffer_3_out[5], controlled_buffer_3_out[6], controlled_buffer_3_out[7]);
  Button button_2 (.out(button_2_out));
  D_Flip_Flop d_ff_2 (.D(or_11_out), .clk(or_12_out), .Q(d_ff_2_q), .reset(button_2_out));  // open: Qn, preset
  or or_11 (or_11_out, and_7_out, and_9_out);
  or or_12 (or_12_out, and_6_out, and_8_out);
  and and_8 (and_8_out, or_4_out, clock_1_out);
  nor nor_3 (nor_3_out, counter_2_q[0], counter_2_q[1], counter_2_q[2], counter_2_q[3], counter_2_q[4], counter_2_q[5], counter_2_q[6], counter_2_q[7]);
  xor xor_1 (xor_1_out, register_1_q[0], d_ff_1_q);
  and and_9 (and_9_out, nor_3_out, or_4_out);
  and and_10 (and_10_out, register_1_q[2], xor_1_out);
  or or_13 (or_13_out, and_10_out, and_11_out);
  xor xor_2 (xor_2_out, register_1_q[1], d_ff_2_q);
  D_Flip_Flop d_ff_3 (
    .D(or_13_out), .clk(demultiplexer_2_out7), .Q(d_ff_3_q), .reset(button_2_out));  // open: Qn, preset
  and and_11 (and_11_out, register_1_q[3], xor_2_out);

  // Notes on the sheet:
  //   contents of rom_1 (hex, n*v repeats v):
  //   0 2 0 8c 8 7 6 5 ff 13 0 a 0 4 6 4 496*0 48 65 6c 6c 6f 20 57 6f 72 6c 64 20 66 72 6f 6d 20 74 68 65
  //   20 61 73 73 65 6d 62 6c 65 72 21 a 4e 6f 77 20 69 74 20 63 61 6e 20 68 61 6e 64 6c 65 20 2c 2e 22 5c
  //   20 61 6e 64 20 74 68 65 20 6f 74 68 65 72 20 73 74 75 66 66 a
endmodule
